# Fritzing sketch UNO_MEGA (saved by Fritzing 0.9.3b)

parts:
  Part1 = Arduino Uno (Rev3)
  Part2 = Arduino Mega 2560 (Rev3)

nets:
  N1: Part1.D10_PWM/SS, Part2.D53
  N2: Part1.D11_PWM/MOSI, Part2.D51
  N3: Part1.D12/MISO, Part2.D50
  N4: Part1.D13/SCK, Part2.D52
